// Logisim project Single-Cycle-CPU.circ as structural Verilog
module Datapath (
  input  in_1,
  output out_2
);

  wire and_1_out, clock_1_out, control_unit_1_alusrc, control_unit_1_branch, control_unit_1_jump,
       control_unit_1_memreg, control_unit_1_no_op, control_unit_1_out_5, control_unit_1_out_6,
       control_unit_1_out_7, control_unit_1_regdest, n20_bit_alu_minimized_1_out_8;
  wire [1:0] control_unit_1_aluop1;
  wire [2:0] alu_control_1_out;
  wire [3:0] multiplexer_1_out;
  wire [4:0] bit_extender_4_out;
  wire [16:0] shifter_1_out;
  wire [18:0] adder_1_out;
  wire [19:0] adder_2_out, bit_extender_1_out, bit_extender_2_out, bit_extender_3_out, multiplexer_2_out,
       multiplexer_3_out, multiplexer_4_out, multiplexer_5_out, n20_bit_alu_minimized_1_out_6, ram_1_data,
       register_1_q, register_file_1_out_8, register_file_1_out_9, rom_1_data, shifter_2_out;

  Register #(.width(20)) register_1 (
    .D(multiplexer_4_out), .Q(register_1_q), .clk(clock_1_out), .clr(in_1));  // open: en
  Clock clock_1 (.out(clock_1_out));
  assign bit_extender_1_out = {{19{1'b0}}, 1'b1};  // Bit_Extender bit_extender_1
  Adder #(.width(20)) adder_1 (
    .a(bit_extender_1_out), .b(register_1_q), .out({bit_extender_3_out[19], adder_1_out}));  // open: cin, cout
  ROM #(.addrWidth(20), .dataWidth(20)) rom_1 (.addr(register_1_q), .data(rom_1_data));  // open: sel
  Multiplexer #(.width(4), .enable("false")) multiplexer_1 (
    .in0(rom_1_data[12:9]), .in1(rom_1_data[8:5]), .out(multiplexer_1_out), .sel(control_unit_1_regdest));
  Shifter #(.width(17)) shifter_1 (
    .in({rom_1_data[16:5], rom_1_data[3], rom_1_data[4], rom_1_data[2:0]}), .\dist (5'b00010),
    .out(shifter_1_out));
  Control_Unit control_unit_1 (
    .in_1(rom_1_data[19:17]), .RegDest(control_unit_1_regdest), .ALUSrc(control_unit_1_alusrc),
    .MemReg(control_unit_1_memreg), .out_5(control_unit_1_out_5), .out_6(control_unit_1_out_6),
    .out_7(control_unit_1_out_7), .Branch(control_unit_1_branch), .Jump(control_unit_1_jump),
    .No_op(control_unit_1_no_op), .ALUop0(control_unit_1_aluop1[1]), .ALUOp1(control_unit_1_aluop1[0]));
  assign bit_extender_2_out = {{11{1'b0}}, {rom_1_data[2:0], rom_1_data[3], rom_1_data[4], rom_1_data[8:5]}};  // Bit_Extender bit_extender_2
  assign bit_extender_3_out[18:0] = {{2{1'b0}}, shifter_1_out};  // Bit_Extender bit_extender_3
  Register_File register_file_1 (
    .out_8(register_file_1_out_8), .out_9(register_file_1_out_9), .Write_Register(multiplexer_1_out),
    .in_3(control_unit_1_out_5), .in_7(multiplexer_5_out), .CLK(clock_1_out), .CLR(in_1),
    .in_1(rom_1_data[16:13]), .in_2(rom_1_data[12:9]));
  assign bit_extender_4_out = {{3{1'b0}}, {rom_1_data[3], rom_1_data[4]}};  // Bit_Extender bit_extender_4
  Multiplexer #(.width(20), .enable("false")) multiplexer_2 (
    .in0(register_file_1_out_9), .in1(bit_extender_2_out), .out(multiplexer_2_out),
    .sel(control_unit_1_alusrc));
  Shifter #(.width(20)) shifter_2 (.in(bit_extender_2_out), .\dist (5'b00010), .out(shifter_2_out));
  ALU_Control alu_control_1 (.Out(alu_control_1_out), .Funct(rom_1_data[2:0]), .in_2(control_unit_1_aluop1));
  Adder #(.width(20)) adder_2 (
    .a({bit_extender_3_out[19], adder_1_out}), .b(shifter_2_out), .out(adder_2_out));  // open: cin, cout
  // Probe on n20_bit_alu_minimized_1_out_6
  _20_bit_ALU__Minimized u_20_bit_alu_minimized_1 (
    .out_6(n20_bit_alu_minimized_1_out_6), .Cout(out_2), .in_1(register_file_1_out_8),
    .shamt(multiplexer_2_out), .in_3(bit_extender_4_out), .ALUopt(alu_control_1_out),
    .out_8(n20_bit_alu_minimized_1_out_8), .NOPs(control_unit_1_no_op));
  and and_1 (and_1_out, control_unit_1_branch, n20_bit_alu_minimized_1_out_8);
  Multiplexer #(.width(20), .enable("false")) multiplexer_3 (
    .in0({bit_extender_3_out[19], adder_1_out}), .in1(adder_2_out), .out(multiplexer_3_out), .sel(and_1_out));
  Multiplexer #(.width(20), .enable("false")) multiplexer_4 (
    .in0(multiplexer_3_out), .in1(bit_extender_3_out), .out(multiplexer_4_out), .sel(control_unit_1_jump));
  RAM #(.addrWidth(20), .dataWidth(20), .bus("separate")) ram_1 (
    .addr(n20_bit_alu_minimized_1_out_6), .din(register_file_1_out_9), .data(ram_1_data),
    .str(control_unit_1_out_7), .clk(clock_1_out), .ld(control_unit_1_out_6), .clr(in_1));  // open: sel
  Multiplexer #(.width(20), .enable("false")) multiplexer_5 (
    .in0(n20_bit_alu_minimized_1_out_6), .in1(ram_1_data), .out(multiplexer_5_out),
    .sel(control_unit_1_memreg));

  // Notes on the sheet:
  //   CLK
  //   contents of rom_1 (hex, n*v repeats v):
  //   c060a c080f a0a04 68e7
  //   op
  //   rs
  //   rt
  //   rd
  //   shamt
  //   funct
  //   CLR
endmodule

// Register File
module Register_File (
  input  [3:0] in_1,
  input  [3:0] in_2,
  input  in_3,
  input  CLK,
  input  CLR,
  input  [3:0] Write_Register,
  input  [19:0] in_7,
  output [19:0] out_8,
  output [19:0] out_9
);

  wire and_1_out, and_2_out, and_3_out, and_4_out, and_5_out, and_6_out, and_7_out, and_8_out, and_9_out,
       and_10_out, and_11_out, and_12_out, and_13_out, and_14_out, and_15_out, and_16_out, decoder_1_out0,
       decoder_1_out1, decoder_1_out2, decoder_1_out3, decoder_1_out4, decoder_1_out5, decoder_1_out6,
       decoder_1_out7, decoder_1_out8, decoder_1_out9, decoder_1_out10, decoder_1_out11, decoder_1_out12,
       decoder_1_out13, decoder_1_out14, decoder_1_out15;
  wire [19:0] r0_q, r1_q, r2_q, r3_q, r4_q, r5_q, r6_q, r7_q, r8_q, r9_q, r10_q, r11_q, r12_q, r13_q, r14_q,
       r15_q;

  Decoder #(.select(4), .enable("false")) decoder_1 (
    .out0(decoder_1_out0), .out1(decoder_1_out1), .out2(decoder_1_out2), .out3(decoder_1_out3),
    .out4(decoder_1_out4), .out5(decoder_1_out5), .out6(decoder_1_out6), .out7(decoder_1_out7),
    .out8(decoder_1_out8), .out9(decoder_1_out9), .out10(decoder_1_out10), .out11(decoder_1_out11),
    .out12(decoder_1_out12), .out13(decoder_1_out13), .out14(decoder_1_out14), .out15(decoder_1_out15),
    .sel(Write_Register));
  and and_1 (and_1_out, decoder_1_out0, ~in_3);  // AND_Gate
  and and_2 (and_2_out, decoder_1_out1, in_3);
  and and_3 (and_3_out, decoder_1_out2, in_3);
  and and_4 (and_4_out, decoder_1_out3, in_3);
  and and_5 (and_5_out, decoder_1_out4, in_3);
  and and_6 (and_6_out, decoder_1_out5, in_3);
  and and_7 (and_7_out, decoder_1_out6, in_3);
  and and_8 (and_8_out, decoder_1_out7, in_3);
  Register #(.width(20)) r0 (.D(in_7), .en(and_1_out), .Q(r0_q), .clk(CLK), .clr(CLR));
  Register #(.width(20)) r1 (.D(in_7), .en(and_2_out), .Q(r1_q), .clk(CLK), .clr(CLR));
  Register #(.width(20)) r2 (.D(in_7), .en(and_3_out), .Q(r2_q), .clk(CLK), .clr(CLR));
  Register #(.width(20)) r3 (.D(in_7), .en(and_4_out), .Q(r3_q), .clk(CLK), .clr(CLR));
  Register #(.width(20)) r4 (.D(in_7), .en(and_5_out), .Q(r4_q), .clk(CLK), .clr(CLR));
  Register #(.width(20)) r5 (.D(in_7), .en(and_6_out), .Q(r5_q), .clk(CLK), .clr(CLR));
  Register #(.width(20)) r6 (.D(in_7), .en(and_7_out), .Q(r6_q), .clk(CLK), .clr(CLR));
  Register #(.width(20)) r7 (.D(in_7), .en(and_8_out), .Q(r7_q), .clk(CLK), .clr(CLR));
  and and_9 (and_9_out, decoder_1_out8, in_3);
  and and_10 (and_10_out, decoder_1_out9, in_3);
  and and_11 (and_11_out, decoder_1_out10, in_3);
  and and_12 (and_12_out, decoder_1_out11, in_3);
  and and_13 (and_13_out, decoder_1_out12, in_3);
  and and_14 (and_14_out, decoder_1_out13, in_3);
  and and_15 (and_15_out, decoder_1_out14, in_3);
  and and_16 (and_16_out, decoder_1_out15, in_3);
  Register #(.width(20)) r8 (.D(in_7), .en(and_9_out), .Q(r8_q), .clk(CLK), .clr(CLR));
  Register #(.width(20)) r9 (.D(in_7), .en(and_10_out), .Q(r9_q), .clk(CLK), .clr(CLR));
  Register #(.width(20)) r10 (.D(in_7), .en(and_11_out), .Q(r10_q), .clk(CLK), .clr(CLR));
  Register #(.width(20)) r11 (.D(in_7), .en(and_12_out), .Q(r11_q), .clk(CLK), .clr(CLR));
  Register #(.width(20)) r12 (.D(in_7), .en(and_13_out), .Q(r12_q), .clk(CLK), .clr(CLR));
  Register #(.width(20)) r13 (.D(in_7), .en(and_14_out), .Q(r13_q), .clk(CLK), .clr(CLR));
  Register #(.width(20)) r14 (.D(in_7), .en(and_15_out), .Q(r14_q), .clk(CLK), .clr(CLR));
  Register #(.width(20)) r15 (.D(in_7), .en(and_16_out), .Q(r15_q), .clk(CLK), .clr(CLR));
  Multiplexer #(.select(4), .width(20), .enable("false")) multiplexer_1 (
    .in0(r0_q), .in1(r1_q), .in2(r2_q), .in3(r3_q), .in4(r4_q), .in5(r5_q), .in6(r6_q), .in7(r7_q),
    .in8(r8_q), .in9(r9_q), .in10(r10_q), .in11(r11_q), .in12(r12_q), .in13(r13_q), .in14(r14_q),
    .in15(r15_q), .out(out_8), .sel(in_1));
  Multiplexer #(.select(4), .width(20), .enable("false")) multiplexer_2 (
    .in0(r0_q), .in1(r1_q), .in2(r2_q), .in3(r3_q), .in4(r4_q), .in5(r5_q), .in6(r6_q), .in7(r7_q),
    .in8(r8_q), .in9(r9_q), .in10(r10_q), .in11(r11_q), .in12(r12_q), .in13(r13_q), .in14(r14_q),
    .in15(r15_q), .out(out_9), .sel(in_2));

  // Notes on the sheet:
  //   Write Control
  //   Write Data
  //   Read Register 2
  //   Read Data 1
  //   Read Register 1
  //   Read Data 2
endmodule

module Control_Unit (
  input  [2:0] in_1,
  output RegDest,
  output ALUSrc,
  output MemReg,
  output out_5,
  output out_6,
  output out_7,
  output Branch,
  output Jump,
  output No_op,
  output ALUop0,
  output ALUOp1
);

  wire and_3_out, and_4_out, and_6_out;

  and and_1 (RegDest, ~in_1[2], ~in_1[1], ~in_1[0]);  // AND_Gate
  and and_2 (out_7, ~in_1[2], ~in_1[1], in_1[0]);  // AND_Gate
  and and_3 (and_3_out, ~in_1[2], in_1[1], ~in_1[0]);  // AND_Gate
  and and_4 (and_4_out, ~in_1[2], in_1[1], in_1[0]);  // AND_Gate
  and and_5 (No_op, in_1[2], ~in_1[1], ~in_1[0]);  // AND_Gate
  and and_6 (and_6_out, in_1[2], ~in_1[1], in_1[0]);  // AND_Gate
  and and_7 (MemReg, in_1[2], in_1[1], ~in_1[0]);  // AND_Gate
  and and_8 (Jump, in_1[2], in_1[1], in_1[0]);
  or or_1 (ALUSrc, out_7, and_6_out, MemReg);
  or or_2 (out_5, RegDest, and_6_out, MemReg);
  or or_3 (ALUop0, and_4_out, and_3_out);
  or or_4 (ALUOp1, No_op, RegDest);

  assign Branch = ALUop0;
  assign out_6 = MemReg;

  // Notes on the sheet:
  //   Opcode
  //   R-type
  //   SW
  //   BNE
  //   BEQ
  //   NOP
  //   ADDi
  //   LW
  //   JMP
  //   RegWrite
  //   MemRead
  //   MemWrite
endmodule

module ALU_Control (
  input  [2:0] Funct,
  input  [1:0] in_2,
  output [2:0] Out
);

  wire and_1_out, not_1_out;

  not not_1 (not_1_out, in_2[1]);
  and and_1 (and_1_out, Funct[2], in_2[1]);
  or or_1 (Out[0], Funct[0], not_1_out);
  or or_2 (Out[1], Funct[1], not_1_out);
  or or_3 (Out[2], and_1_out, in_2[0]);

  // Notes on the sheet:
  //   ALUop
endmodule

module _1_bit_ALU (
  input  A,
  input  B,
  input  shamt,
  input  Less,
  input  Cin,
  input  [2:0] in_6,
  input  Binv,
  output out_8,
  output Cout,
  output SET
);

  wire and_1_out, multiplexer_1_out, nor_1_out, not_1_out, or_1_out, shifter_1_out, shifter_2_out;

  not not_1 (not_1_out, B);
  Shifter #(.width(1)) shifter_1 (.in(shamt), .\dist (A), .out(shifter_1_out));
  Shifter #(.width(1), .shift("lr")) shifter_2 (.in(shamt), .\dist (A), .out(shifter_2_out));
  Multiplexer #(.enable("false")) multiplexer_1 (.in0(B), .in1(not_1_out), .out(multiplexer_1_out), .sel(Binv));
  or or_1 (or_1_out, A, B);
  nor nor_1 (nor_1_out, A, B);
  and and_1 (and_1_out, A, B);
  Adder #(.width(1)) adder_1 (.a(A), .b(multiplexer_1_out), .out(SET), .cin(Cin), .cout(Cout));
  Multiplexer #(.select(3), .enable("false")) multiplexer_2 (
    .in0(shifter_1_out), .in1(Less), .in2(shifter_2_out), .in3(SET), .in4(or_1_out), .in5(nor_1_out),
    .in6(and_1_out), .in7(SET), .out(out_8), .sel(in_6));

  // Notes on the sheet:
  //   ALUopt
  //   Out
endmodule

module _20_bit_ALU (
  input  Shamt,
  input  [2:0] ALUOpt,
  input  [19:0] in_3,
  input  [19:0] in_4,
  output [19:0] out_5,
  output out_6,
  output Cout
);

  wire and_1_out, n1_bit_alu_1_set, n1_bit_alu_2_cout, n1_bit_alu_3_cout, n1_bit_alu_4_cout,
       n1_bit_alu_5_cout, n1_bit_alu_6_cout, n1_bit_alu_7_cout, n1_bit_alu_8_cout, n1_bit_alu_9_cout,
       n1_bit_alu_10_cout, n1_bit_alu_11_cout, n1_bit_alu_12_cout, n1_bit_alu_13_cout, n1_bit_alu_14_cout,
       n1_bit_alu_15_cout, n1_bit_alu_16_cout, n1_bit_alu_17_cout, n1_bit_alu_18_cout, n1_bit_alu_19_cout,
       n1_bit_alu_20_cout, xnor_1_out;

  and and_1 (and_1_out, xnor_1_out, ALUOpt[0]);
  xnor xnor_1 (xnor_1_out, ALUOpt[2], ALUOpt[1]);
  _1_bit_ALU u_1_bit_alu_1 (
    .Cin(n1_bit_alu_3_cout), .out_8(out_5[19]), .Cout(Cout), .SET(n1_bit_alu_1_set), .A(in_4[19]),
    .B(in_3[19]), .Less(n1_bit_alu_1_set), .Binv(and_1_out), .in_6(ALUOpt), .shamt(Shamt));
  _1_bit_ALU u_1_bit_alu_2 (
    .Cin(and_1_out), .out_8(out_5[0]), .Cout(n1_bit_alu_2_cout), .A(in_4[0]), .B(in_3[0]),
    .Less(n1_bit_alu_1_set), .Binv(and_1_out), .in_6(ALUOpt), .shamt(Shamt));  // open: SET
  _1_bit_ALU u_1_bit_alu_3 (
    .Cin(n1_bit_alu_6_cout), .out_8(out_5[18]), .Cout(n1_bit_alu_3_cout), .A(in_4[18]), .B(in_3[18]),
    .Less(n1_bit_alu_1_set), .Binv(and_1_out), .in_6(ALUOpt), .shamt(Shamt));  // open: SET
  _1_bit_ALU u_1_bit_alu_4 (
    .Cin(n1_bit_alu_2_cout), .out_8(out_5[1]), .Cout(n1_bit_alu_4_cout), .A(in_4[1]), .B(in_3[1]),
    .Less(n1_bit_alu_1_set), .Binv(and_1_out), .in_6(ALUOpt), .shamt(Shamt));  // open: SET
  _1_bit_ALU u_1_bit_alu_5 (
    .Cin(n1_bit_alu_4_cout), .out_8(out_5[2]), .Cout(n1_bit_alu_5_cout), .A(in_4[2]), .B(in_3[2]),
    .Less(n1_bit_alu_1_set), .Binv(and_1_out), .in_6(ALUOpt), .shamt(Shamt));  // open: SET
  _1_bit_ALU u_1_bit_alu_6 (
    .Cin(n1_bit_alu_8_cout), .out_8(out_5[17]), .Cout(n1_bit_alu_6_cout), .A(in_4[17]), .B(in_3[17]),
    .Less(n1_bit_alu_1_set), .Binv(and_1_out), .in_6(ALUOpt), .shamt(Shamt));  // open: SET
  _1_bit_ALU u_1_bit_alu_7 (
    .Cin(n1_bit_alu_5_cout), .out_8(out_5[3]), .Cout(n1_bit_alu_7_cout), .A(in_4[3]), .B(in_3[3]),
    .Less(n1_bit_alu_1_set), .Binv(and_1_out), .in_6(ALUOpt), .shamt(Shamt));  // open: SET
  _1_bit_ALU u_1_bit_alu_8 (
    .Cin(n1_bit_alu_10_cout), .out_8(out_5[16]), .Cout(n1_bit_alu_8_cout), .A(in_4[16]), .B(in_3[16]),
    .Less(n1_bit_alu_1_set), .Binv(and_1_out), .in_6(ALUOpt), .shamt(Shamt));  // open: SET
  _1_bit_ALU u_1_bit_alu_9 (
    .Cin(n1_bit_alu_7_cout), .out_8(out_5[4]), .Cout(n1_bit_alu_9_cout), .A(in_4[4]), .B(in_3[4]),
    .Less(n1_bit_alu_1_set), .Binv(and_1_out), .in_6(ALUOpt), .shamt(Shamt));  // open: SET
  _1_bit_ALU u_1_bit_alu_10 (
    .Cin(n1_bit_alu_12_cout), .out_8(out_5[15]), .Cout(n1_bit_alu_10_cout), .A(in_4[15]), .B(in_3[15]),
    .Less(n1_bit_alu_1_set), .Binv(and_1_out), .in_6(ALUOpt), .shamt(Shamt));  // open: SET
  _1_bit_ALU u_1_bit_alu_11 (
    .Cin(n1_bit_alu_9_cout), .out_8(out_5[5]), .Cout(n1_bit_alu_11_cout), .A(in_4[5]), .B(in_3[5]),
    .Less(n1_bit_alu_1_set), .Binv(and_1_out), .in_6(ALUOpt), .shamt(Shamt));  // open: SET
  _1_bit_ALU u_1_bit_alu_12 (
    .Cin(n1_bit_alu_14_cout), .out_8(out_5[14]), .Cout(n1_bit_alu_12_cout), .A(in_4[14]), .B(in_3[14]),
    .Less(n1_bit_alu_1_set), .Binv(and_1_out), .in_6(ALUOpt), .shamt(Shamt));  // open: SET
  _1_bit_ALU u_1_bit_alu_13 (
    .Cin(n1_bit_alu_11_cout), .out_8(out_5[6]), .Cout(n1_bit_alu_13_cout), .A(in_4[6]), .B(in_3[6]),
    .Less(n1_bit_alu_1_set), .Binv(and_1_out), .in_6(ALUOpt), .shamt(Shamt));  // open: SET
  _1_bit_ALU u_1_bit_alu_14 (
    .Cin(n1_bit_alu_16_cout), .out_8(out_5[13]), .Cout(n1_bit_alu_14_cout), .A(in_4[13]), .B(in_3[13]),
    .Less(n1_bit_alu_1_set), .Binv(and_1_out), .in_6(ALUOpt), .shamt(Shamt));  // open: SET
  _1_bit_ALU u_1_bit_alu_15 (
    .Cin(n1_bit_alu_13_cout), .out_8(out_5[7]), .Cout(n1_bit_alu_15_cout), .A(in_4[7]), .B(in_3[7]),
    .Less(n1_bit_alu_1_set), .Binv(and_1_out), .in_6(ALUOpt), .shamt(Shamt));  // open: SET
  _1_bit_ALU u_1_bit_alu_16 (
    .Cin(n1_bit_alu_18_cout), .out_8(out_5[12]), .Cout(n1_bit_alu_16_cout), .A(in_4[12]), .B(in_3[12]),
    .Less(n1_bit_alu_1_set), .Binv(and_1_out), .in_6(ALUOpt), .shamt(Shamt));  // open: SET
  _1_bit_ALU u_1_bit_alu_17 (
    .Cin(n1_bit_alu_15_cout), .out_8(out_5[8]), .Cout(n1_bit_alu_17_cout), .A(in_4[8]), .B(in_3[8]),
    .Less(n1_bit_alu_1_set), .Binv(and_1_out), .in_6(ALUOpt), .shamt(Shamt));  // open: SET
  _1_bit_ALU u_1_bit_alu_18 (
    .Cin(n1_bit_alu_19_cout), .out_8(out_5[11]), .Cout(n1_bit_alu_18_cout), .A(in_4[11]), .B(in_3[11]),
    .Less(n1_bit_alu_1_set), .Binv(and_1_out), .in_6(ALUOpt), .shamt(Shamt));  // open: SET
  _1_bit_ALU u_1_bit_alu_19 (
    .Cin(n1_bit_alu_20_cout), .out_8(out_5[10]), .Cout(n1_bit_alu_19_cout), .A(in_4[10]), .B(in_3[10]),
    .Less(n1_bit_alu_1_set), .Binv(and_1_out), .in_6(ALUOpt), .shamt(Shamt));  // open: SET
  _1_bit_ALU u_1_bit_alu_20 (
    .Cin(n1_bit_alu_17_cout), .out_8(out_5[9]), .Cout(n1_bit_alu_20_cout), .A(in_4[9]), .B(in_3[9]),
    .Less(n1_bit_alu_1_set), .Binv(and_1_out), .in_6(ALUOpt), .shamt(Shamt));  // open: SET
  nor nor_1 (out_6, out_5[19], out_5[18], out_5[17], out_5[16], out_5[15], out_5[14], out_5[13], out_5[12], out_5[11], out_5[10], out_5[9], out_5[8], out_5[7], out_5[6], out_5[5], out_5[4], out_5[3], out_5[2], out_5[1], out_5[0]);

  // Notes on the sheet:
  //   A
  //   B
  //   Zero Flag
  //   Out
endmodule

// 20-bit ALU
module _20_bit_ALU__Minimized (
  input  [19:0] in_1,
  input  [19:0] shamt,
  input  [4:0] in_3,
  input  NOPs,
  input  [2:0] ALUopt,
  output [19:0] out_6,
  output Cout,
  output out_8
);

  wire and_2_out, xnor_1_out;
  wire [4:0] multiplexer_1_out;
  wire [19:0] adder_1_out, and_1_out, msb_check_1_out_2, multiplexer_2_out, nor_1_out, not_1_out, or_1_out,
       shifter_1_out, shifter_2_out;

  assign not_1_out = ~shamt;  // NOT_Gate not_1, 20 bits wide
  Multiplexer #(.width(5), .enable("false")) multiplexer_1 (
    .in0({5{1'b0}}), .in1(in_3), .out(multiplexer_1_out), .sel(NOPs));
  Multiplexer #(.width(20), .enable("false")) multiplexer_2 (
    .in0(shamt), .in1(not_1_out), .out(multiplexer_2_out), .sel(and_2_out));
  Shifter #(.width(20)) shifter_1 (.in(in_1), .\dist (multiplexer_1_out), .out(shifter_1_out));
  Shifter #(.width(20), .shift("lr")) shifter_2 (.in(in_1), .\dist (in_3), .out(shifter_2_out));
  Adder #(.width(20)) adder_1 (.a(in_1), .b(multiplexer_2_out), .out(adder_1_out), .cin(and_2_out), .cout(Cout));
  assign or_1_out = in_1 | shamt;  // OR_Gate or_1, 20 bits wide
  assign nor_1_out = ~(in_1 | shamt);  // NOR_Gate nor_1, 20 bits wide
  assign and_1_out = in_1 & shamt;  // AND_Gate and_1, 20 bits wide
  and and_2 (and_2_out, ALUopt[0], xnor_1_out);
  xnor xnor_1 (xnor_1_out, ALUopt[1], ALUopt[2]);
  Multiplexer #(.select(3), .width(20), .enable("false")) multiplexer_3 (
    .in0(shifter_1_out), .in1(msb_check_1_out_2), .in2(shifter_2_out), .in3(adder_1_out), .in4(or_1_out),
    .in5(nor_1_out), .in6(and_1_out), .in7(adder_1_out), .out(out_6), .sel(ALUopt));
  MSB_Check msb_check_1 (.in_1(adder_1_out), .out_2(msb_check_1_out_2));
  nor nor_2 (out_8, out_6[19], out_6[18], out_6[17], out_6[16], out_6[15], out_6[14], out_6[13], out_6[12], out_6[11], out_6[10], out_6[9], out_6[8], out_6[7], out_6[6], out_6[5], out_6[4], out_6[3], out_6[2], out_6[1], out_6[0]);

  // Notes on the sheet:
  //   A
  //   B
  //   Binv
  //   Zero Flag
  //   Out
endmodule

module MSB_Check (
  input  [19:0] in_1,
  output [19:0] out_2
);

  assign out_2 = {{19{1'b0}}, in_1[19]};  // Bit_Extender bit_extender_1

  // Notes on the sheet:
  //   SET
  //   LESS
endmodule

module Datapath3 (
  input  in_1
);

  wire and_1_out, and_2_out, clock_1_out, control_unit_1_alusrc, control_unit_1_branch, control_unit_1_jump,
       control_unit_1_memreg, control_unit_1_no_op, control_unit_1_out_5, control_unit_1_out_6,
       control_unit_1_out_7, control_unit_1_regdest, n20_bit_alu_minimized_1_out_8;
  wire [1:0] control_unit_1_aluop1;
  wire [2:0] alu_control_1_out;
  wire [3:0] multiplexer_1_out;
  wire [4:0] bit_extender_4_out;
  wire [19:0] adder_1_out, bit_extender_1_out, bit_extender_2_out, bit_extender_3_out, multiplexer_2_out,
       multiplexer_3_out, multiplexer_4_out, multiplexer_5_out, multiplexer_6_out,
       n20_bit_alu_minimized_1_out_6, ram_1_data, register_1_q, register_file_1_out_8, register_file_1_out_9,
       rom_1_data;

  Register #(.width(20)) register_1 (
    .D(multiplexer_5_out), .Q(register_1_q), .clk(clock_1_out), .clr(in_1));  // open: en
  assign bit_extender_1_out = {{19{1'b0}}, 1'b1};  // Bit_Extender bit_extender_1
  Clock clock_1 (.out(clock_1_out));
  Adder #(.width(20)) adder_1 (.a(bit_extender_1_out), .b(register_1_q), .out(adder_1_out));  // open: cin, cout
  ROM #(.addrWidth(20), .dataWidth(20)) rom_1 (.addr(register_1_q), .data(rom_1_data));  // open: sel
  Multiplexer #(.width(4), .enable("false")) multiplexer_1 (
    .in0(rom_1_data[12:9]), .in1(rom_1_data[8:5]), .out(multiplexer_1_out), .sel(control_unit_1_regdest));
  assign bit_extender_2_out = {{3{1'b0}}, {rom_1_data[16:5], rom_1_data[3], rom_1_data[4], rom_1_data[2:0]}};  // Bit_Extender bit_extender_2
  Control_Unit control_unit_1 (
    .in_1(rom_1_data[19:17]), .RegDest(control_unit_1_regdest), .ALUSrc(control_unit_1_alusrc),
    .MemReg(control_unit_1_memreg), .out_5(control_unit_1_out_5), .out_6(control_unit_1_out_6),
    .out_7(control_unit_1_out_7), .Branch(control_unit_1_branch), .Jump(control_unit_1_jump),
    .No_op(control_unit_1_no_op), .ALUop0(control_unit_1_aluop1[1]), .ALUOp1(control_unit_1_aluop1[0]));
  assign bit_extender_3_out = {{11{1'b0}}, {rom_1_data[2:0], rom_1_data[3], rom_1_data[4], rom_1_data[8:5]}};  // Bit_Extender bit_extender_3
  Register_File register_file_1 (
    .out_8(register_file_1_out_8), .out_9(register_file_1_out_9), .Write_Register(multiplexer_1_out),
    .in_3(control_unit_1_out_5), .in_7(multiplexer_6_out), .CLK(clock_1_out), .CLR(in_1),
    .in_1(rom_1_data[16:13]), .in_2(rom_1_data[12:9]));
  assign bit_extender_4_out = {{3{1'b0}}, {rom_1_data[3], rom_1_data[4]}};  // Bit_Extender bit_extender_4
  Multiplexer #(.width(20), .enable("false")) multiplexer_2 (
    .in0(register_file_1_out_9), .in1(bit_extender_3_out), .out(multiplexer_2_out),
    .sel(control_unit_1_alusrc));
  ALU_Control alu_control_1 (.Out(alu_control_1_out), .Funct(rom_1_data[2:0]), .in_2(control_unit_1_aluop1));
  and and_1 (and_1_out, control_unit_1_branch, n20_bit_alu_minimized_1_out_8);
  _20_bit_ALU__Minimized u_20_bit_alu_minimized_1 (
    .out_6(n20_bit_alu_minimized_1_out_6), .in_1(register_file_1_out_8), .shamt(multiplexer_2_out),
    .in_3(bit_extender_4_out), .ALUopt(alu_control_1_out), .out_8(n20_bit_alu_minimized_1_out_8),
    .NOPs(control_unit_1_no_op));  // open: Cout
  Multiplexer #(.width(20), .enable("false")) multiplexer_3 (
    .in0(adder_1_out), .in1(bit_extender_3_out), .out(multiplexer_3_out), .sel(and_1_out));
  and and_2 (and_2_out, control_unit_1_branch, ~n20_bit_alu_minimized_1_out_8);  // AND_Gate
  Multiplexer #(.width(20), .enable("false")) multiplexer_4 (
    .in0(multiplexer_3_out), .in1(bit_extender_3_out), .out(multiplexer_4_out), .sel(and_2_out));
  Multiplexer #(.width(20), .enable("false")) multiplexer_5 (
    .in0(multiplexer_4_out), .in1(bit_extender_2_out), .out(multiplexer_5_out), .sel(control_unit_1_jump));
  RAM #(.addrWidth(20), .dataWidth(20), .bus("separate")) ram_1 (
    .addr(n20_bit_alu_minimized_1_out_6), .din(register_file_1_out_9), .data(ram_1_data),
    .str(control_unit_1_out_7), .clk(clock_1_out), .ld(control_unit_1_out_6), .clr(in_1));  // open: sel
  Multiplexer #(.width(20), .enable("false")) multiplexer_6 (
    .in0(n20_bit_alu_minimized_1_out_6), .in1(ram_1_data), .out(multiplexer_6_out),
    .sel(control_unit_1_memreg));

  // Notes on the sheet:
  //   CLK
  //   contents of rom_1 (hex, n*v repeats v):
  //   a2203 4427 a2203 8887 a8802 28a0
  //   op
  //   rs
  //   rt
  //   rd
  //   shamt
  //   funct
endmodule

module Datapath4 (
  input  in_1
);

  wire and_1_out, clock_1_out, control_unit_1_alusrc, control_unit_1_branch, control_unit_1_jump,
       control_unit_1_memreg, control_unit_1_no_op, control_unit_1_out_5, control_unit_1_out_6,
       control_unit_1_out_7, control_unit_1_regdest, n20_bit_alu_minimized_1_p5;
  wire [1:0] control_unit_1_aluop1;
  wire [2:0] n20_bit_alu_minimized_1_p4;
  wire [3:0] multiplexer_1_out;
  wire [4:0] bit_extender_4_out;
  wire [19:0] adder_1_out, bit_extender_1_out, bit_extender_2_out, bit_extender_3_out, multiplexer_2_out,
       multiplexer_3_out, multiplexer_4_out, multiplexer_5_out, n20_bit_alu_minimized_1_p6, ram_1_data,
       register_1_q, register_file_1_out_8, register_file_1_out_9, rom_1_data;

  Clock clock_1 (.out(clock_1_out));
  assign bit_extender_1_out = {{19{1'b0}}, 1'b1};  // Bit_Extender bit_extender_1
  Register #(.width(20)) register_1 (
    .D(multiplexer_4_out), .Q(register_1_q), .clk(clock_1_out), .clr(in_1));  // open: en
  Adder #(.width(20)) adder_1 (.a(bit_extender_1_out), .b(register_1_q), .out(adder_1_out));  // open: cin, cout
  ROM #(.addrWidth(20), .dataWidth(20)) rom_1 (.addr(register_1_q), .data(rom_1_data));  // open: sel
  assign bit_extender_2_out = {{3{1'b0}}, rom_1_data[16:0]};  // Bit_Extender bit_extender_2
  Multiplexer #(.width(4), .enable("false")) multiplexer_1 (
    .in0(rom_1_data[12:9]), .in1(rom_1_data[8:5]), .out(multiplexer_1_out), .sel(control_unit_1_regdest));
  assign bit_extender_3_out = {{11{1'b0}}, rom_1_data[8:0]};  // Bit_Extender bit_extender_3
  Control_Unit control_unit_1 (
    .in_1(rom_1_data[19:17]), .RegDest(control_unit_1_regdest), .ALUSrc(control_unit_1_alusrc),
    .MemReg(control_unit_1_memreg), .out_5(control_unit_1_out_5), .out_6(control_unit_1_out_6),
    .out_7(control_unit_1_out_7), .Branch(control_unit_1_branch), .Jump(control_unit_1_jump),
    .No_op(control_unit_1_no_op), .ALUop0(control_unit_1_aluop1[1]), .ALUOp1(control_unit_1_aluop1[0]));
  assign bit_extender_4_out = {{3{1'b0}}, {rom_1_data[3], rom_1_data[4]}};  // Bit_Extender bit_extender_4
  Register_File register_file_1 (
    .out_8(register_file_1_out_8), .out_9(register_file_1_out_9), .Write_Register(multiplexer_1_out),
    .in_3(control_unit_1_out_5), .in_7(multiplexer_5_out), .CLK(clock_1_out), .CLR(in_1),
    .in_1(rom_1_data[16:13]), .in_2(rom_1_data[12:9]));
  Multiplexer #(.width(20), .enable("false")) multiplexer_2 (
    .in0(register_file_1_out_9), .in1(bit_extender_3_out), .out(multiplexer_2_out),
    .sel(control_unit_1_alusrc));
  // _20_bit_ALU__Minimized 20_bit_alu_minimized_1: pin names not known; wires that end beside it: register_file_1_out_8, multiplexer_2_out, bit_extender_4_out, n20_bit_alu_minimized_1_p4, n20_bit_alu_minimized_1_p5, n20_bit_alu_minimized_1_p6, control_unit_1_no_op
  ALU_Control alu_control_1 (.Out(n20_bit_alu_minimized_1_p4), .Funct(rom_1_data[2:0]), .in_2(control_unit_1_aluop1));
  and and_1 (and_1_out, control_unit_1_branch, n20_bit_alu_minimized_1_p5);
  Multiplexer #(.width(20), .enable("false")) multiplexer_3 (
    .in0(adder_1_out), .in1(bit_extender_3_out), .out(multiplexer_3_out), .sel(and_1_out));
  RAM #(.addrWidth(20), .dataWidth(20), .bus("separate")) ram_1 (
    .addr(n20_bit_alu_minimized_1_p6), .din(register_file_1_out_9), .data(ram_1_data),
    .str(control_unit_1_out_7), .clk(clock_1_out), .ld(control_unit_1_out_6), .clr(in_1));  // open: sel
  Multiplexer #(.width(20), .enable("false")) multiplexer_4 (
    .in0(multiplexer_3_out), .in1(bit_extender_2_out), .out(multiplexer_4_out), .sel(control_unit_1_jump));
  Multiplexer #(.width(20), .enable("false")) multiplexer_5 (
    .in0(n20_bit_alu_minimized_1_p6), .in1(ram_1_data), .out(multiplexer_5_out), .sel(control_unit_1_memreg));

  // Notes on the sheet:
  //   contents of rom_1 (hex, n*v repeats v):
  //   a2203 4427 a2203 8887 a8802 28a0
  //   op
  //   rs
  //   rt
  //   rd
  //   shamt
  //   funct
endmodule

module Datapath5 (
  input  Branch,
  input  MemtoReg,
  input  RegWrite,
  input  ALUSrc,
  input  MemWrite,
  input  MemRead
);

  wire and_1_out, clock_1_out, n20_bit_alu_minimized_1_out_8;
  wire [3:0] multiplexer_1_out;
  wire [4:0] bit_extender_3_out;
  wire [19:0] adder_1_out, adder_2_out, bit_extender_1_out, bit_extender_2_out, multiplexer_2_out,
       multiplexer_3_out, multiplexer_4_out, n20_bit_alu_minimized_1_out_6, ram_1_data, register_1_q,
       register_file_1_out_8, register_file_1_out_9, rom_1_data;

  Register #(.width(20)) register_1 (.D(multiplexer_3_out), .Q(register_1_q), .clk(clock_1_out));  // open: en, clr
  Clock clock_1 (.out(clock_1_out));
  assign bit_extender_1_out = {{19{1'b0}}, 1'b1};  // Bit_Extender bit_extender_1
  Adder #(.width(20)) adder_1 (.a(bit_extender_1_out), .b(register_1_q), .out(adder_1_out));  // open: cin, cout
  ROM #(.addrWidth(20), .dataWidth(20)) rom_1 (.addr(register_1_q), .data(rom_1_data));  // open: sel
  Multiplexer #(.width(4), .enable("false")) multiplexer_1 (
    .in0(rom_1_data[11:8]), .in1(rom_1_data[15:12]), .out(multiplexer_1_out), .sel(RegWrite));
  assign bit_extender_2_out = {{12{1'b0}}, rom_1_data[19:12]};  // Bit_Extender bit_extender_2
  assign bit_extender_3_out = {{1{1'b0}}, rom_1_data[19:16]};  // Bit_Extender bit_extender_3
  Register_File register_file_1 (
    .out_8(register_file_1_out_8), .out_9(register_file_1_out_9), .Write_Register(multiplexer_1_out),
    .in_7(multiplexer_4_out), .CLK(clock_1_out), .in_1(rom_1_data[7:4]), .in_2(rom_1_data[11:8]));  // open: in_3, CLR
  Multiplexer #(.width(20), .enable("false")) multiplexer_2 (
    .in0(register_file_1_out_9), .in1(bit_extender_2_out), .out(multiplexer_2_out), .sel(ALUSrc));
  _20_bit_ALU__Minimized u_20_bit_alu_minimized_1 (
    .out_6(n20_bit_alu_minimized_1_out_6), .in_1(register_file_1_out_8), .shamt(multiplexer_2_out),
    .in_3(bit_extender_3_out), .out_8(n20_bit_alu_minimized_1_out_8));  // open: Cout, ALUopt, NOPs
  Adder #(.width(20)) adder_2 (.a(adder_1_out), .b(bit_extender_2_out), .out(adder_2_out));  // open: cin, cout
  and and_1 (and_1_out, Branch, n20_bit_alu_minimized_1_out_8);
  Multiplexer #(.width(20), .enable("false")) multiplexer_3 (
    .in0(adder_1_out), .in1(adder_2_out), .out(multiplexer_3_out), .sel(and_1_out));
  RAM #(.addrWidth(20), .dataWidth(20), .bus("separate")) ram_1 (
    .addr(n20_bit_alu_minimized_1_out_6), .din(register_file_1_out_9), .data(ram_1_data), .str(MemWrite),
    .clk(clock_1_out), .ld(MemRead));  // open: sel, clr
  Multiplexer #(.width(20), .enable("false")) multiplexer_4 (
    .in0(n20_bit_alu_minimized_1_out_6), .in1(ram_1_data), .out(multiplexer_4_out), .sel(MemtoReg));

  // Notes on the sheet:
  //   ADD,SRL, SUB, OR, NAND, SLL, ADDI, BEQ
  //   RS
  //   RT
  //   RD
  //   SHAMT
  //   immediate value
endmodule
